# Fritzing sketch soil_measurement_sketch (saved by Fritzing 0.9.3b)
breadboards: 1

parts:
  Bauteil1 = Arduino Nano (Rev3.0)
  U1 = ATTINY45 [package=dip]
  U2 = FS1000A - 433Mhz RF Transmitter [package=THT]
  U3 = XD-RF-5V [package=THT]
  LED1 = LED - 5mm [color="Green (570nm)" package="5 mm [THT]"]
  R1 = Resistor [tolerance=±2% resistance=220 package=THT]
  C1 = Electrolytic Capacitor [capacitance=10µF voltage=50V package="100 mil [THT, electrolytic]"]
  C3 = Ceramic Capacitor [capacitance=100nF voltage=16V package="100 mil [THT, multilayer]"]
  C4 = Ceramic Capacitor [capacitance=100nF voltage=16V package="100 mil [THT, multilayer]"]
  C5 = Electrolytic Capacitor [capacitance=10µF voltage=50V package="100 mil [THT, electrolytic]"]
  ANT1 = Antenna
  ANT2 = Antenna
  LED2 = LED - 5mm [color="Green (570nm)" package="5 mm [THT]"]
  LED3 = LED - 5mm [color="Red (635nm)" package="5 mm [THT]"]
  R2 = Resistor [tolerance=±2% resistance=220 package=THT]
  R3 = Resistor [tolerance=±2% resistance=220 package=THT]

nets:
  N1: Bauteil1.D5, LED1.anode
  N2: Bauteil1.D11/MOSI, U3.DATA#1
  N3: U1.PB4(ADC2), U2.DATA
  GND: U1.GND, U2.GND, U3.GND, R1.Pin_0, C1.-, C1.+, C3.0, C3.1, R2.Pin_1, R3.Pin_1
  N4: U1.PB0(MOSI), LED2.anode
  N5: U1.PB1(MISO), LED3.anode
  VCC: U1.VCC, U2.VCC, U3.VCC, C4.0, C4.1, C5.-, C5.+
  N6: U2.Antenna, ANT1.antenna_lead
  N7: U3.Attenna, ANT2.antenna_lead
  N8: LED1.cathode, R1.Pin_1
  N9: LED2.cathode, R3.Pin_0
  N10: LED3.cathode, R2.Pin_0

custom parts:
  FS1000A - 433Mhz RF Transmitter: This is 433Mhz RF transmitter with receiver kit for Arduino ARM MCU wireless Application environment: Remote control switch, receiver module, motorcycles, automobile anti-theft products, home security products, electric doors, shutter doors, windows, remote control socket, remote control LED, remote audio remote control electric doors, garage door remote control, remote control retractable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
  XD-RF-5V: This is 433Mhz RF transmitter with receiver kit for Arduino ARM MCU wireless Application environment: Remote control switch, receiver module, motorcycles, automobile anti-theft products, home security products, electric doors, shutter doors, windows, remote control socket, remote control LED, remote audio remote control electric doors, garage door remote control, remote control retractable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
